# Fritzing sketch AD8402_Test (saved by Fritzing 0.9.3b)
breadboards: 1

parts:
  U1 = mystery part, 14 pins [chip_label=AD8402]
  R1 = Resistor [tolerance=±5% resistance=1k package=THT]
  LED1 = LED - 5mm [color="Red (633nm)" package="5 mm [THT]"]
  R2 = Resistor [tolerance=±5% resistance=1k package=THT]
  LED2 = LED - 5mm [color="Red (633nm)" package="5 mm [THT]"]
  パーツ1 = Arduino Uno (Rev3)
  C1 = Electrolytic Capacitor [capacitance=1µF package="100 mil [THT, electrolytic]"]
  C2 = Ceramic Capacitor [capacitance=100nF package="100 mil [THT, multilayer]"]

nets:
  N1: U1.pin1, U1.pin2, U1.pin5, U1.pin14, LED1.cathode, LED2.cathode, パーツ1.GND, C1.-, C2.1
  N2: U1.pin3, U1.pin6, U1.pin10, U1.pin11, U1.pin13, パーツ1.5V, C1.+, C2.0
  N3: U1.pin4, R2.Pin_1
  N4: U1.pin7, パーツ1.D10_PWM/SS
  N5: U1.pin8, パーツ1.D11_PWM/MOSI
  N6: U1.pin9, パーツ1.D13/SCK
  N7: U1.pin12, R1.Pin_1
  N8: R1.Pin_0, LED1.anode
  N9: R2.Pin_0, LED2.anode

notes:
  AD8402
  1 AGND 14 B1
  2 B2 13 A1
  3 A2 12 W1
  4 W2 11 VDD
  5 DGND 10 !RS
  6 !SDN 9 CLK
  7 !CS 8 SDI
