# Fritzing sketch AD8402_WeinBridge_DCO_Test (saved by Fritzing 0.9.3b)
breadboards: 2

parts:
  U1 = mystery part, 3 pins [chip_label=TLE2426]
  C1 = Electrolytic Capacitor [capacitance=1µF package="100 mil [THT, electrolytic]"]
  C2 = Electrolytic Capacitor [capacitance=1µF package="100 mil [THT, electrolytic]"]
  C3 = Electrolytic Capacitor [capacitance=1µF package="100 mil [THT, electrolytic]"]
  IC1 = Dual Op-Amp [package=dip08]
  D1 = Rectifier Diode [part_number=1N4001 package="300 mil [THT]"]
  D2 = Rectifier Diode [part_number=1N4001 package="300 mil [THT]"]
  R2 = Resistor [tolerance=±5% resistance=10k package=THT]
  R1 = Resistor [tolerance=±5% resistance=100k package=THT]
  R3 = Resistor [tolerance=±5% resistance=2.2k package=THT]
  R4 = TRIMPOT [package=3362u-2]
  C4 = Film/Foil Capacitor [capacitance=100nF voltage=35V package="5mm [THT, pp]"]
  C5 = Film/Foil Capacitor [capacitance=100nF voltage=35V package="5mm [THT, pp]"]
  C6 = Electrolytic Capacitor [capacitance=1µF package="100 mil [THT, electrolytic]"]
  R5 = Resistor [tolerance=±5% resistance=100k package=THT]
  R6 = Resistor [tolerance=±5% resistance=10k package=THT]
  U2 = mystery part, 14 pins [chip_label=AD8402/10]
  C7 = Ceramic Capacitor [capacitance=100nF package="100 mil [THT, multilayer]"]
  C8 = Ceramic Capacitor [capacitance=100nF package="100 mil [THT, multilayer]"]
  C9 = Ceramic Capacitor [capacitance=100nF package="100 mil [THT, multilayer]"]
  パーツ1 = Arduino Uno (Rev3)
  R7 = Resistor [tolerance=±5% resistance=1k package=THT]
  LED1 = LED - 3mm [color="Green (570nm)" package="3 mm [THT]"]
  R8 = Rotary Potentiometer (Small) [maximum_resistance=100kΩ package=THT]

nets:
  N1: U1.pin1, C2.-, C3.+, R4.WIPER, R4.CW, C5.+, U2.pin14, C7.0, C8.1
  N2: U1.pin2, C1.-, C3.-, IC1.A_V-, R5.Pin_1, R6.Pin_1, U2.pin1, U2.pin5, C8.0, C9.1, パーツ1.GND, LED1.cathode, R8.leg1
  N3: C1.+, C2.+, IC1.A_V+, U2.pin6, U2.pin10, U2.pin11, C7.1, C9.0, パーツ1.5V, R7.Pin_0, R8.leg2
  N4: IC1.A_OUT, IC1.B_+IN, D1.anode, D2.cathode, R2.Pin_1, U2.pin3, U2.pin4
  N5: IC1.A_-IN, R2.Pin_0, R1.Pin_0, R3.Pin_0
  N6: IC1.A_+IN, C4.-, C5.-, U2.pin12, U2.pin13
  N7: IC1.B_-IN, IC1.B_OUT, C6.+
  N8: D1.cathode, D2.anode, R1.Pin_1
  N9: R3.Pin_1, R4.CCW
  N10: C4.+, U2.pin2
  N11: C6.-, R5.Pin_0, R6.Pin_0
  N12: U2.pin7, パーツ1.D10_PWM/SS
  N13: U2.pin8, パーツ1.D11_PWM/MOSI
  N14: U2.pin9, パーツ1.D13/SCK
  N15: パーツ1.A0, R8.wiper
  N16: R7.Pin_1, LED1.anode

notes:
  VGND
  +5V
  GND
  VGND
  AD8402
  1 AGND 14 B1
  2 B2 13 A1
  3 A2 12 W1
  4 W2 11 VDD
  5 DGND 10 !RS
  6 !SDN 9 CLK
  7 !CS 8 SDI
  GND
  +5V
  OUT
