# Fritzing sketch Wein Bridge_NJM2137 (saved by Fritzing 0.9.3b)
breadboards: 1

parts:
  IC1 = Dual Op-Amp [package=dip08]
  D1 = Rectifier Diode [part_number=1N4001 package="300 mil [THT]"]
  D2 = Rectifier Diode [part_number=1N4001 package="300 mil [THT]"]
  R1 = Resistor [tolerance=±5% resistance=10k package=THT]
  R2 = Resistor [tolerance=±5% resistance=100k package=THT]
  R3 = Resistor [tolerance=±5% resistance=2.2k package=THT]
  C1 = Film/Foil Capacitor [capacitance=100nF voltage=35V package="5mm [THT, pp]"]
  C2 = Film/Foil Capacitor [capacitance=100nF voltage=35V package="5mm [THT, pp]"]
  R6 = Resistor [tolerance=±5% resistance=10k package=THT]
  C3 = Ceramic Capacitor [capacitance=100nF package="100 mil [THT, multilayer]"]
  C4 = Ceramic Capacitor [capacitance=100nF package="100 mil [THT, multilayer]"]
  C5 = Electrolytic Capacitor [capacitance=1µF package="100 mil [THT, electrolytic]"]
  C6 = Electrolytic Capacitor [capacitance=1µF package="100 mil [THT, electrolytic]"]
  R7 = Rotary Potentiometer (Small) [maximum_resistance=100kΩ package=THT]
  R8 = Rotary Potentiometer (Small) [maximum_resistance=100kΩ package=THT]
  U1 = mystery part, 6 pins [chip_label="Trim 5k"]

nets:
  N1: IC1.A_OUT, D1.anode, D2.cathode, R1.Pin_1, R6.Pin_0, R8.leg1
  N2: IC1.A_-IN, R1.Pin_0, R2.Pin_0, R3.Pin_1
  N3: IC1.A_+IN, C1.-, C2.-, R7.wiper, R7.leg2
  N4: IC1.A_V-, C4.0, C6.-
  N5: IC1.B_+IN, C2.+, R6.Pin_1, C3.0, C4.1, C5.-, C6.+, R7.leg1, U1.pin4, U1.pin6
  N6: IC1.B_-IN, IC1.B_OUT
  N7: IC1.A_V+, C3.1, C5.+
  N8: D1.cathode, D2.anode, R2.Pin_1
  N9: R3.Pin_0, U1.pin1
  N10: C1.+, R8.wiper, R8.leg2

notes:
  -2.5V
  GND
  GND
  +2.5V
  OUT
  C: 0.47uF
  Wein Bridge
  33.8Hz～
  10k DPDT
