# Fritzing sketch Wein Bridge_NJM2137_AD8403_10ohm (saved by Fritzing 0.9.3b)
breadboards: 2

parts:
  IC1 = Dual Op-Amp [package=dip08]
  D1 = Rectifier Diode [part_number=1N4001 package="300 mil [THT]"]
  D2 = Rectifier Diode [part_number=1N4001 package="300 mil [THT]"]
  R1 = Resistor [tolerance=±5% resistance=10k package=THT]
  R2 = Resistor [tolerance=±5% resistance=100k package=THT]
  R3 = Resistor [tolerance=±5% resistance=47k package=THT]
  C1 = Film/Foil Capacitor [capacitance=100nF voltage=35V package="5mm [THT, pp]"]
  C2 = Film/Foil Capacitor [capacitance=100nF voltage=35V package="5mm [THT, pp]"]
  R6 = Resistor [tolerance=±5% resistance=10k package=THT]
  C3 = Ceramic Capacitor [capacitance=100nF package="100 mil [THT, multilayer]"]
  C4 = Ceramic Capacitor [capacitance=100nF package="100 mil [THT, multilayer]"]
  C5 = Electrolytic Capacitor [capacitance=1µF package="100 mil [THT, electrolytic]"]
  C6 = Electrolytic Capacitor [capacitance=1µF package="100 mil [THT, electrolytic]"]
  U1 = mystery part, 24 pins [chip_label=AD803/10k]
  C7 = Ceramic Capacitor [capacitance=100nF package="100 mil [THT, multilayer]"]
  パーツ1 = Arduino Uno (Rev3)
  C8 = Electrolytic Capacitor [capacitance=1µF package="100 mil [THT, electrolytic]"]
  R7 = Rotary Potentiometer (Small) [maximum_resistance=100kΩ package=THT]

nets:
  N1: IC1.A_OUT, D1.anode, D2.cathode, R1.Pin_1, R6.Pin_0, U1.pin18, U1.pin19
  N2: IC1.A_-IN, R1.Pin_0, R2.Pin_0, R3.Pin_0
  N3: IC1.A_+IN, C1.-, C2.-, U1.pin22, U1.pin23
  N4: IC1.A_V-, C4.0, C6.-, U1.pin1, U1.pin5, U1.pin9, U1.pin17, U1.pin21, C7.1, パーツ1.GND, C8.-, R7.leg1
  N5: IC1.B_+IN, R3.Pin_1, C2.+, R6.Pin_1, C3.0, C4.1, C5.-, C6.+, U1.pin24
  N6: IC1.B_-IN, IC1.B_OUT
  N7: IC1.A_V+, C3.1, C5.+
  N8: D1.cathode, D2.anode, R2.Pin_1
  N9: C1.+, U1.pin20
  N10: U1.pin10, U1.pin15, U1.pin16, C7.0, パーツ1.5V, C8.+
  N11: U1.pin11, パーツ1.D10_PWM/SS
  N12: U1.pin12, パーツ1.D11_PWM/MOSI
  N13: U1.pin14, パーツ1.D13/SCK
  N14: パーツ1.A0, R7.wiper

notes:
  -2.5V
  GND
  GND
  +2.5V
  OUT
  C: 0.47uF
  Wein Bridge
  340Hz
