# Fritzing sketch Wein Bridge_NJM2137_AD8403_10ohm_VoltageFollower (saved by Fritzing 0.9.3b)
breadboards: 4

parts:
  U1 = mystery part, 24 pins [chip_label=AD803/10k]
  C7 = Ceramic Capacitor [capacitance=100nF package="100 mil [THT, multilayer]"]
  パーツ1 = Arduino Uno (Rev3)
  C8 = Electrolytic Capacitor [capacitance=1µF package="100 mil [THT, electrolytic]"]
  R7 = Rotary Potentiometer (Small) [maximum_resistance=100kΩ package=THT]
  U2 = mystery part, 6 pins [chip_label="Trim 5k"]
  IC2 = Dual Op-Amp [package=dip08]
  D3 = Rectifier Diode [part_number=1N4001 package="300 mil [THT]"]
  D4 = Rectifier Diode [part_number=1N4001 package="300 mil [THT]"]
  R11 = Resistor [tolerance=±5% resistance=10k package=THT]
  R12 = Resistor [tolerance=±5% resistance=100k package=THT]
  R13 = Resistor [tolerance=±5% resistance=2.2k package=THT]
  C9 = Film/Foil Capacitor [capacitance=100nF voltage=35V package="5mm [THT, pp]"]
  C10 = Film/Foil Capacitor [capacitance=100nF voltage=35V package="5mm [THT, pp]"]
  C11 = Ceramic Capacitor [capacitance=100nF package="100 mil [THT, multilayer]"]
  C12 = Ceramic Capacitor [capacitance=100nF package="100 mil [THT, multilayer]"]
  C13 = Electrolytic Capacitor [capacitance=1µF package="100 mil [THT, electrolytic]"]
  C14 = Electrolytic Capacitor [capacitance=1µF package="100 mil [THT, electrolytic]"]
  U3 = mystery part, 3 pins [chip_label=2426]
  R14 = Resistor [tolerance=±5% resistance=10k package=THT]
  C15 = Electrolytic Capacitor [capacitance=1µF package="100 mil [THT, electrolytic]"]
  U4 = mystery part, 3 pins [chip_label=EMIFIL]

nets:
  N1: U1.pin1, U1.pin5, U1.pin9, U1.pin17, U1.pin21, U1.pin24, C7.1, パーツ1.GND, C8.-, R7.leg1, IC2.A_V-, C12.0, C14.-, U3.pin2, R14.Pin_1, U4.pin2
  N2: U1.pin10, U1.pin15, U1.pin16, C7.0, パーツ1.5V, C8.+, IC2.A_V+, C11.1, C13.+, U3.pin3
  N3: U1.pin11, パーツ1.D10_PWM/SS
  N4: U1.pin12, パーツ1.D11_PWM/MOSI
  N5: U1.pin14, パーツ1.D13/SCK
  N6: U1.pin18, U1.pin19, IC2.A_OUT, IC2.B_+IN, D3.cathode, D4.anode, R11.Pin_1
  N7: U1.pin20, C9.+
  N8: U1.pin22, U1.pin23, IC2.A_+IN, C9.-, C10.-
  N9: パーツ1.A0, R7.wiper
  N10: U2.pin1, R13.Pin_0
  N11: U2.pin4, U2.pin6, C10.+, C11.0, C12.1, C13.-, C14.+, U3.pin1
  N12: IC2.A_-IN, R11.Pin_0, R12.Pin_0, R13.Pin_1
  N13: IC2.B_-IN, IC2.B_OUT, U4.pin1
  N14: D3.anode, D4.cathode, R12.Pin_1
  N15: R14.Pin_0, C15.-
  N16: C15.+, U4.pin3

notes:
  GND
  VGND
  VGND
  +5V
  OUT
  C: 0.47uF
  Wein Bridge
  33.8Hz～
  GND
  +5V
  Rail Splitter
  AC Coupling
  10uF 10k-ohm
